# Fritzing sketch schematic (saved by Fritzing 0.9.9b)
breadboards: 1

parts:
  R1 = Resistor [tolerance=±5% power=0.25 resistance=10k package=THT]
  DHT1 = DHT22 Humidity and Temperature Sensor
  Bauteil1 = Adafruit HUZZAH ESP8266 [part_number="Adafruit #2471"]  # not connected

nets:
  N1: R1.Pin_0, DHT1.VDD
  N2: R1.Pin_1, DHT1.DATA

custom parts:
  Adafruit HUZZAH ESP8266: Add Internet to your next project with an adorable, bite-sized WiFi microcontroller, at a price you like! The ESP8266 processor from Espressif is an 80 MHz microcontroller with a full WiFi front-end (both as client and access point) and TCP/IP stack with DNS support as well. While this chip has been very popular, its also been very difficult to use. Most of the low cost modules are not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
